# Fritzing sketch shield_mega (saved by Fritzing 0.9.3b)
circuit board: 5.31284cm x 8.55134cm
breadboards: 1

parts:
  220Ω = Resistor [tolerance=±5% resistance=220 package=THT]
  Thêta_plateform_shield = Arduino Mega 2560 (Rev3)
  Right_Motor = Stepper Motor - Bipolar
  Left_Motor = Stepper Motor - Bipolar
  ESP8266 = ESP8266 WiFi Module [part_number=ESP8266]
  LED = LED - 5mm [color="Red (633nm)" package="5 mm [THT]"]
  100µF = Capacitor Polarized [package=cpol-radial-100uf-25v]
  100µF_2 = Capacitor Polarized [package=cpol-radial-100uf-25v]
  Power = Power Jack [package=power_jack_slot]
  NPN_Transistor = NPN-Transistor [package="TO92 [THT]"]
  10KΩ = Resistor [tolerance=±5% resistance=10k package=THT]
  Pololu_A4988 = A4988 Stepper Motor Driver Carrier
  Pololu_A4988_2 = A4988 Stepper Motor Driver Carrier

nets:
  N1: 220Ω.Pin_0, LED.anode
  N2: 220Ω.Pin_1, Thêta_plateform_shield.D13_PWM
  N3: Thêta_plateform_shield.D15/RX3, ESP8266.TXD
  N4: Thêta_plateform_shield.D14/TX3, ESP8266.RXD
  GND: Thêta_plateform_shield.GND, ESP8266.GND, LED.cathode, 100µF.-, 100µF_2.-, Power.GNDBREAK, Power.GND, NPN_Transistor.E, Pololu_A4988.GROUND, Pololu_A4988_2.GROUND
  3V3: Thêta_plateform_shield.3V3, ESP8266.VCC, ESP8266.CH_PD
  N5: Thêta_plateform_shield.VIN, 100µF.+, 100µF_2.+, Power.PWR, Pololu_A4988.VMOT, Pololu_A4988_2.VMOT
  N6: Thêta_plateform_shield.D6_PWM, 10KΩ.Pin_1
  VDD: Thêta_plateform_shield.5V, Pololu_A4988.VDD, Pololu_A4988_2.VDD
  N7: Thêta_plateform_shield.D22, Pololu_A4988.DIR
  N8: Thêta_plateform_shield.D24, Pololu_A4988.STEP
  N9: Thêta_plateform_shield.D26, Pololu_A4988.MS3
  N10: Thêta_plateform_shield.D28, Pololu_A4988.MS2
  N11: Thêta_plateform_shield.D30, Pololu_A4988.MS1
  N12: Thêta_plateform_shield.D32, Pololu_A4988.Enable
  N13: Thêta_plateform_shield.D42, Pololu_A4988_2.DIR
  N14: Thêta_plateform_shield.D44, Pololu_A4988_2.STEP
  N15: Thêta_plateform_shield.D46, Pololu_A4988_2.MS3
  N16: Thêta_plateform_shield.D48, Pololu_A4988_2.MS2
  N17: Thêta_plateform_shield.D50, Pololu_A4988_2.MS1
  N18: Thêta_plateform_shield.D52, Pololu_A4988_2.Enable
  N19: Right_Motor.A, Pololu_A4988_2.OUT_2B
  N20: Right_Motor.C, Pololu_A4988_2.OUT_2A
  N21: Right_Motor.B, Pololu_A4988_2.OUT_1A
  N22: Right_Motor.D, Pololu_A4988_2.OUT_1B
  N23: Left_Motor.A, Pololu_A4988.OUT_2B
  N24: Left_Motor.C, Pololu_A4988.OUT_2A
  N25: Left_Motor.B, Pololu_A4988.OUT_1A
  N26: Left_Motor.D, Pololu_A4988.OUT_1B
  N27: ESP8266.RST, NPN_Transistor.C
  N28: NPN_Transistor.B, 10KΩ.Pin_0
  N29: Pololu_A4988.RESET, Pololu_A4988.SLEEP
  N30: Pololu_A4988_2.RESET, Pololu_A4988_2.SLEEP

notes:
  12V power supply via jack connector.
  Capacitors 100uF
  LED +
  220 Ohms resistor
  ESP8266 : Wifi module
  Motor Driver
  NEMA 17 Motors
  NEMA 17 Motors (9V, 1.65A)
  12V output
  Wifi reset transistor

custom parts:
  ESP8266 WiFi Module: Generic WiFi Module based on the ESP8266 with onboard PCB antenna and UART communications
  Capacitor Polarized: Capacitor Polarized These are standard SMD and PTH capacitors. Normally 10uF, 47uF, and 100uF in electrolytic and tantalum varieties. Always verify the external diameter of the through hole cap, it varies with capacity, voltage, and manufacturer. The EIA devices should be standard.
  A4988 Stepper Motor Driver Carrier: The Pololu stepper motor driver carrier for the A4988 motor driver integrated circuits. http://www.pololu.com/catalog/product/1182
