# Fritzing sketch laser_scheme (saved by Fritzing 0.9.3b)
circuit board: 5.31cm x 5.55666cm
breadboards: 1

parts:
  ESP8266_wifi_shield = Arduino Uno (Rev3) - ICSP
  NPN_Transistor = NPN-Transistor [package="TO92 [THT]"]
  10KΩ = Resistor [tolerance=±5% resistance=10k package=THT]
  ESP8266 = ESP8266 WiFi Module [part_number=ESP8266]
  LED1 = LED - 5mm [color="Red (633nm)" package="5 mm [THT]"]
  220Ω1 = Resistor [tolerance=±5% resistance=220 package=THT]
  J2 = female pin header, 3 pins [form="♀ (female)"]
  J3 = female pin header, 3 pins [form="♀ (female)"]
  J1 = male pin header, 2 pins [form="♂ (male)"]

nets:
  N1: ESP8266_wifi_shield.ICSP_SCK, ESP8266_wifi_shield.D13/SCK, LED1.anode
  N2: ESP8266_wifi_shield.GND, NPN_Transistor.E, 220Ω1.Pin_1
  N3: ESP8266_wifi_shield.D0/RX, J3.pin3
  N4: ESP8266_wifi_shield.D1/TX, J2.pin3
  N5: ESP8266_wifi_shield.D2, J2.pin1
  N6: ESP8266_wifi_shield.D3_PWM, J3.pin1
  N7: ESP8266_wifi_shield.D7, 10KΩ.Pin_0
  3V3: ESP8266_wifi_shield.3V3, ESP8266.VCC, ESP8266.CH_PD
  N8: NPN_Transistor.B, 10KΩ.Pin_1
  N9: NPN_Transistor.C, ESP8266.RST
  N10: ESP8266.RXD, J2.pin2
  N11: ESP8266.GPIO_0, J1.pin2
  N12: ESP8266.GPIO_2, J1.pin1
  N13: ESP8266.TXD, J3.pin2
  N14: LED1.cathode, 220Ω1.Pin_0

custom parts:
  ESP8266 WiFi Module: Generic WiFi Module based on the ESP8266 with onboard PCB antenna and UART communications
