# Fritzing sketch sensors_cable (saved by Fritzing 0.9.3b)
circuit board: 5.92842cm x 3.63762cm

parts:
  J17 = double row female pin header, 36 pins [form="♀ (female)"]
  J1 = female pin header, 5 pins [form="♀ (female)"]
  J29 = female pin header, 5 pins [form="♀ (female)"]
  J30 = female pin header, 5 pins [form="♀ (female)"]
  J31 = female pin header, 5 pins [form="♀ (female)"]
  J32 = female pin header, 5 pins [form="♀ (female)"]
  J33 = female pin header, 5 pins [form="♀ (female)"]
  J34 = female pin header, 5 pins [form="♀ (female)"]
  J35 = female pin header, 5 pins [form="♀ (female)"]
  J36 = female pin header, 5 pins [form="♀ (female)"]
  J37 = female pin header, 5 pins [form="♀ (female)"]

nets:
  N1: J17.pin1, J17.pin36, J1.pin1, J29.pin1, J30.pin1, J31.pin1, J32.pin1, J33.pin1, J34.pin1, J35.pin1, J36.pin1, J37.pin1
  N2: J17.pin8, J36.pin3
  N3: J17.pin9, J36.pin2
  N4: J17.pin10, J37.pin3
  N5: J17.pin11, J37.pin2
  N6: J17.pin19, J1.pin4, J1.pin5
  N7: J17.pin20, J1.pin3
  N8: J17.pin21, J1.pin2
  N9: J17.pin22, J29.pin3
  N10: J17.pin23, J29.pin2
  N11: J17.pin24, J31.pin3
  N12: J17.pin25, J31.pin2
  N13: J17.pin26, J30.pin3
  N14: J17.pin27, J30.pin2
  N15: J17.pin28, J32.pin3
  N16: J17.pin29, J32.pin2
  N17: J17.pin30, J34.pin3
  N18: J17.pin31, J34.pin2
  N19: J17.pin32, J35.pin3
  N20: J17.pin33, J35.pin2
  N21: J17.pin34, J33.pin3
  N22: J17.pin35, J33.pin2
  N23: J29.pin4, J29.pin5
  N24: J30.pin4, J30.pin5
  N25: J31.pin4, J31.pin5
  N26: J32.pin4, J32.pin5
  N27: J33.pin4, J33.pin5
  N28: J34.pin4, J34.pin5
  N29: J35.pin4, J35.pin5
  N30: J36.pin4, J36.pin5
  N31: J37.pin4, J37.pin5
